# Fritzing sketch Esquema eletrico (saved by Fritzing 0.9.10b)

parts:
  Mod1 = Arduino Sensor Shield v5.0
  Componente1 = Arduino Uno (Rev3) - ICSP
  J1 = Basic Servo
  J2 = Basic Servo
  HC-SR04_Sensor_1 = HC-SR04 Ultrasonic Distance Sensor
  HC-SR04_Sensor_2 = HC-SR04 Ultrasonic Distance Sensor
  HC-SR04_Sensor_3 = HC-SR04 Ultrasonic Distance Sensor
  HC-SR04_Sensor_4 = HC-SR04 Ultrasonic Distance Sensor
  M1 = fc-51 [package=THT]
  M2 = fc-51 [package=THT]
  S1 = Round Pushbutton
  BAT1 = BC9VPC [package=bc9vpc]  # not connected
  U1 = LIPO-2000mAh [package=lipo-2000]

nets:
  VCC: Mod1.VCC, Mod1.URF01-VCC, Mod1.A0-VCC, Mod1.A1-VCC, Mod1.A4-VCC, Mod1.A5-VCC, Mod1.AREF-V, Mod1.11-V, Mod1.10-V, Mod1.3-V, Mod1.2-V, Mod1.ParallelLCD-VCC, J1.vcc, J2.vcc, HC-SR04_Sensor_1.VCC, HC-SR04_Sensor_2.VCC, HC-SR04_Sensor_3.VCC, HC-SR04_Sensor_4.VCC, M1.pin3, M2.pin3
  GND: Mod1.SD-GND, Mod1.GND, Mod1.A0-GND, Mod1.A1-GND, Mod1.A4-GND, Mod1.A5-GND, Mod1.APC220-GND, Mod1.11-G, Mod1.10-G, Mod1.3-G, Mod1.2-G, Mod1.ParallelLCD-GND, Mod1.SerialLCD-GND, Componente1.RESET, J1.gnd, J2.gnd, HC-SR04_Sensor_1.GND, HC-SR04_Sensor_2.GND, HC-SR04_Sensor_3.GND, HC-SR04_Sensor_4.GND, M1.pin2, M2.pin2
  N1: Mod1.SD-D11, Mod1.11-S, J2.pulse
  N2: Mod1.URF01-A0, Mod1.A0-SIG, HC-SR04_Sensor_4.TRIG
  N3: Mod1.URF01-A1, Mod1.A1-SIG, HC-SR04_Sensor_4.ECHO
  N4: Mod1.A2-SIG, HC-SR04_Sensor_2.TRIG
  N5: Mod1.A3-SIG, HC-SR04_Sensor_2.ECHO
  N6: Mod1.A4-SIG, HC-SR04_Sensor_3.TRIG
  N7: Mod1.A5-SIG, HC-SR04_Sensor_3.ECHO
  N8: Mod1.10-S, Mod1.ParallelLCD-D10, J1.pulse
  N9: Mod1.7-S, Mod1.ParallelLCD-D7, HC-SR04_Sensor_1.ECHO
  N10: Mod1.6-S, Mod1.ParallelLCD-D6, HC-SR04_Sensor_1.TRIG
  N11: Mod1.3-S, Mod1.SerialLCD-D3, M1.pin1
  N12: Mod1.2-S, Mod1.SerialLCD-D2, M2.pin1
  N13: S1.leg0, U1.-
